// Logisim project mimo_v04b_AddrBus_Demo.circ as structural Verilog: 2 circuits, main circuit MiMo_v04b_OR
// address
module MiMo_v04b_OR (
  input  [15:0] in_1,
  input  [1:0] addrsel
);

  wire CLK, reset;
  wire [3:0] showhexa_1_digit, showhexa_1_digit_2, showhexa_1_digit_3, showhexa_1_digit_4;
  wire [15:0] address, aluout, immed, sreg;

  Hex_Digit_Display hex_digit_display_1 (.value(showhexa_1_digit));  // open: dp
  ShowHexa showhexa_1 (
    .Digit(showhexa_1_digit), .Digit_2(showhexa_1_digit_2), .Digit_3(showhexa_1_digit_3),
    .Digit_4(showhexa_1_digit_4), .Data(address));
  Hex_Digit_Display hex_digit_display_2 (.value(showhexa_1_digit_2));  // open: dp
  Hex_Digit_Display hex_digit_display_3 (.value(showhexa_1_digit_3));  // open: dp
  Hex_Digit_Display hex_digit_display_4 (.value(showhexa_1_digit_4));  // open: dp
  // Probe on address
  Multiplexer #(.select(2), .width(16), .enable("false")) multiplexer_1 (
    .in0(in_1), .in1(immed), .in2(aluout), .in3(sreg), .out(address), .sel(addrsel));
  // Probe on addrsel
  // Probe on in_1
  Clock Clock (.out(CLK));
  Button u_Reset (.out(reset));

  // Other names for the same wires on the sheet: pc[15:0] = in_1

  // Notes on the sheet:
  //   Address BUS
  //   MiMo - Microprogrammed CPU Model
  //   v0.4b
  //   addrsel: 0..PC 1..IMM 2..ALU 3..Sreg 
  //   OR
  //   PC
endmodule

module ShowHexa (
  input  [15:0] Data,
  output [3:0] Digit,
  output [3:0] Digit_2,
  output [3:0] Digit_3,
  output [3:0] Digit_4
);


  assign Digit = Data[15:12];
  assign Digit_2 = Data[11:8];
  assign Digit_3 = Data[7:4];
  assign Digit_4 = Data[3:0];
endmodule
