// Logisim project mimo_v04b_Control_Unit_Demo.circ as structural Verilog: 1 circuit, main circuit main
module main (
  input  [7:0] Mikro_PC,
  input  Flags,
  input  in_3,
  input  opcode,
  input  [6:0] in_5,
  output [7:0] ucounter,
  output [7:0] out_7
);

  wire CLK, multiplexer_2_out, Ncmd, or_1_out, or_2_out, reset;
  wire [1:0] addrsel, cond;
  wire [3:0] aluop, icycles;
  wire [7:0] multiplexer_1_out, multiplexer_3_out;
  wire [15:0] cycles, DROM;
  wire [31:4] CROM;

  nor nor_1 (Ncmd, Mikro_PC[0], Mikro_PC[1], Mikro_PC[2], Mikro_PC[3], Mikro_PC[5], Mikro_PC[6], Mikro_PC[7], Mikro_PC[4]);
  // Probe on CROM[21:20]
  // Probe on CROM[22]
  // Probe on Mikro_PC
  // Probe on Mikro_PC
  // Probe on CROM[19]
  // Probe on cond
  // Probe on CROM[16:15]
  // Probe on in_5
  // Probe on CROM[13]
  // Probe on CROM[14]
  ROM #(.dataWidth(32)) rom_1 (
    .addr(Mikro_PC), .data({CROM[31:19], cond, CROM[16:9], addrsel, CROM[6:4], aluop}));  // open: sel
  ROM #(.dataWidth(16)) rom_2 (.addr(Mikro_PC), .data(DROM));  // open: sel
  or or_1 (or_1_out, Flags, in_3);
  // Probe on cond
  // Probe on CROM[11]
  // Probe on CROM[12]
  // Probe on DROM[7:0]
  Multiplexer #(.width(8), .enable("false")) multiplexer_1 (
    .in0(DROM[7:0]), .in1(DROM[15:8]), .out(multiplexer_1_out), .sel(multiplexer_2_out));
  // Probe on DROM[15:8]
  Multiplexer #(.select(2), .enable("false")) multiplexer_2 (
    .in0(Flags), .in1(or_1_out), .in2(in_3), .in3(opcode), .out(multiplexer_2_out), .sel(cond));
  Multiplexer #(.width(8), .enable("false")) multiplexer_3 (
    .in0({8{1'b0}}), .in1({1'b0, in_5}), .out(multiplexer_3_out), .sel(CROM[19]));
  // Probe on CROM[10:9]
  // Probe on addrsel
  Adder adder_1 (.a(multiplexer_1_out), .b(multiplexer_3_out), .out(out_7));  // open: cin, cout
  // Probe on out_7
  // Probe on CROM[6]
  // Probe on CROM[5:4]
  // Probe on aluop
  Clock Clock (.out(CLK));
  Counter #(.width(16), .max('hffff), .ongoal("stay")) Cycles_Cnt (
    .Q(cycles), .clk(CLK), .clr(reset));  // open: load, D, count, carry
  Button u_Reset (.out(reset));
  Counter #(.width(4), .max('hf), .ongoal("stay")) Instr_Cycles_Cnt (
    .Q(icycles), .clk(CLK), .clr(or_2_out));  // open: load, D, count, carry
  or or_2 (or_2_out, Ncmd, reset);

  assign ucounter = Mikro_PC;

  // Other names for the same wires on the sheet: opcode_t[6:0] = in_5; c = Flags;
  //   CROM (some bits) = {cond, addrsel, aluop}; op2sel[1:0] = CROM[5:4]; datawrite = CROM[6];
  //   pcsel[1:0] = CROM[10:9]; pcload = CROM[11]; dwrite = CROM[12]; irload = CROM[13]; imload = CROM[14];
  //   regsrc[1:0] = CROM[16:15]; indexsel = CROM[19]; datasel[1:0] = CROM[21:20]; swrite = CROM[22];
  //   MicroPC[7:0] = Mikro_PC; n = opcode; z = in_3

  // Notes on the sheet:
  //   Control ROM
  //   Address of first uinstruction is "opcode+2"
  //   Decision ROM
  //   Micro Instruction
  //   contents of rom_1 (hex, n*v repeats v):
  //   2000 80800 11000 11001 38*0 4000 22*0 1000 0 4000 62*0 40021 1000c0 800 a00
  //   contents of rom_2 (hex, n*v repeats v):
  //   101 202 40*0 8282 22*0 8484 0 8383 62*0 8485 8484
  //   Next uPC
  //   Based on: http://minnie.tuhs.org/Programs/UcodeCPU/index.html
  //   v04: Tidying up model, FB, TTY
  //   v03b: Fix z cond code
  //   Quick tips:
  //   2a [42]:	addrsel=pc  imload=1   # JNEZ Rs,immed
  //   84 [132]:   pcincr:	 pcload=1  pcsel=pc, goto fetch
  //   85 [133]:   jump:	  pcload=1  pcsel=immed, goto fetch
  //   Use ctrl+t to manually toggle global clock signal
  //   41 [65]:	addrsel=pc  dwrite=1  regsrc=databus  # Load immediate Rd, immed
  //   43 [67]:	addrsel=pc  imload=1    # Store Rd into address from immed
  //   82 [130]: aluop=sub  op2sel=const0, if z then pcincr else jump 
  //   Use Simulate->Ticks Enabled for automatic clock signal
  //   2:	aluop=add  op2sel=treg  dwrite=1  regsrc=aluout, goto fetch  # ALU operations on Rd,Rs,Rt
endmodule
