// Logisim project mimo_v04b_RAM_Demo.circ as structural Verilog: 2 circuits, main circuit MiMo_v04b_OR
// address
module MiMo_v04b_OR (
  input  [15:0] in_1,
  input  select,
  input  datawrite,
  input  [1:0] datasel,
  input  [15:0] aluout
);

  wire CLK, not_1_out, reset;
  wire [3:0] showhexa_1_digit, showhexa_1_digit_2, showhexa_1_digit_3, showhexa_1_digit_4, showhexa_2_digit,
       showhexa_2_digit_2, showhexa_2_digit_3, showhexa_2_digit_4;
  wire [15:0] data, dreg, multiplexer_1_out, pc, treg;

  Hex_Digit_Display hex_digit_display_1 (.value(showhexa_1_digit));  // open: dp
  ShowHexa showhexa_1 (
    .Digit(showhexa_1_digit), .Digit_2(showhexa_1_digit_2), .Digit_3(showhexa_1_digit_3),
    .Digit_4(showhexa_1_digit_4), .Data(in_1));
  Hex_Digit_Display hex_digit_display_2 (.value(showhexa_1_digit_3));  // open: dp
  Hex_Digit_Display hex_digit_display_3 (.value(showhexa_1_digit_2));  // open: dp
  Hex_Digit_Display hex_digit_display_4 (.value(showhexa_1_digit_4));  // open: dp
  ShowHexa showhexa_2 (
    .Digit(showhexa_2_digit), .Digit_2(showhexa_2_digit_2), .Digit_3(showhexa_2_digit_3),
    .Digit_4(showhexa_2_digit_4), .Data(data));
  Hex_Digit_Display hex_digit_display_5 (.value(showhexa_2_digit));  // open: dp
  RAM #(.addrWidth(14), .dataWidth(16)) ram_1 (
    .addr(in_1[13:0]), .data(data), .sel(select), .clk(CLK), .ld(not_1_out));  // open: clr
  not not_1 (not_1_out, datawrite);
  Hex_Digit_Display hex_digit_display_6 (.value(showhexa_2_digit_2));  // open: dp
  // Probe on in_1
  Hex_Digit_Display hex_digit_display_7 (.value(showhexa_2_digit_4));  // open: dp
  Hex_Digit_Display hex_digit_display_8 (.value(showhexa_2_digit_3));  // open: dp
  assign data = datawrite ? multiplexer_1_out : 16'bz;  // Controlled_Buffer controlled_buffer_1
  Multiplexer #(.select(2), .width(16), .enable("false")) multiplexer_1 (
    .in0(pc), .in1(dreg), .in2(treg), .in3(aluout), .out(multiplexer_1_out), .sel(datasel));
  // Probe on datasel
  // Probe on aluout
  Clock Clock (.out(CLK));
  Button u_Reset (.out(reset));

  // Other names for the same wires on the sheet: address[15:0] = in_1

  // Notes on the sheet:
  //   Address BUS
  //   RAM
  //   datasel : 0..PC 1..Dreg 2..Treg 3..ALE
  //   MiMo - Microprogrammed CPU Model
  //   Data BUS
  //   v0.4b
  //   OR
endmodule

module ShowHexa (
  input  [15:0] Data,
  output [3:0] Digit,
  output [3:0] Digit_2,
  output [3:0] Digit_3,
  output [3:0] Digit_4
);


  assign Digit = Data[15:12];
  assign Digit_2 = Data[11:8];
  assign Digit_3 = Data[7:4];
  assign Digit_4 = Data[3:0];
endmodule
