// Logisim project mimo_v04b_Registers_Demo.circ as structural Verilog: 3 circuits, main circuit MiMo_v04b_OR
// address
module MiMo_v04b_OR (
  input  dwrite,
  input  swrite,
  input  twrite,
  input  [15:0] Data_Bus,
  input  [15:0] immed,
  input  [15:0] aluout,
  input  [2:0] D_Reg,
  input  [2:0] S_Reg,
  input  [2:0] T_Reg,
  input  [1:0] regsrc,
  output [15:0] dreg,
  output [15:0] sreg,
  output [15:0] treg
);

  wire CLK, reset;
  wire [3:0] showhexa_1_digit, showhexa_1_digit_2, showhexa_1_digit_3, showhexa_1_digit_4;
  wire [15:0] multiplexer_1_out, registerfile_1_r0, registerfile_1_r1, registerfile_1_r2, registerfile_1_r3,
       registerfile_1_r4, registerfile_1_r5, registerfile_1_r6, registerfile_1_r7;

  // Probe on regsrc
  Hex_Digit_Display hex_digit_display_1 (.value(showhexa_1_digit));  // open: dp
  ShowHexa showhexa_1 (
    .Digit(showhexa_1_digit), .Digit_2(showhexa_1_digit_2), .Digit_3(showhexa_1_digit_3),
    .Digit_4(showhexa_1_digit_4), .Data(Data_Bus));
  Hex_Digit_Display hex_digit_display_2 (.value(showhexa_1_digit_2));  // open: dp
  Hex_Digit_Display hex_digit_display_3 (.value(showhexa_1_digit_4));  // open: dp
  Hex_Digit_Display hex_digit_display_4 (.value(showhexa_1_digit_3));  // open: dp
  Multiplexer #(.select(2), .width(16), .enable("false")) multiplexer_1 (
    .in0(Data_Bus), .in1(immed), .in2(aluout), .in3(sreg), .out(multiplexer_1_out), .sel(regsrc));
  // Probe on regsrc
  // Probe on multiplexer_1_out
  // Probe on D_Reg
  // Probe on registerfile_1_r0
  // Probe on registerfile_1_r1
  // Probe on registerfile_1_r2
  // Probe on registerfile_1_r3
  // Probe on registerfile_1_r4
  // Probe on registerfile_1_r5
  // Probe on registerfile_1_r6
  // Probe on registerfile_1_r7
  // Probe on dreg
  // Probe on sreg
  Registerfile registerfile_1 (
    .dwrite(dwrite), .regval(multiplexer_1_out), .sreg(sreg), .treg(treg), .dsel(D_Reg), .ssel(S_Reg),
    .tsel(T_Reg), .r0(registerfile_1_r0), .r1(registerfile_1_r1), .r2(registerfile_1_r2),
    .r7(registerfile_1_r7), .r6(registerfile_1_r6), .r5(registerfile_1_r5), .r4(registerfile_1_r4),
    .r3(registerfile_1_r3), .twrite(twrite), .dreg(dreg), .swrite(swrite), .Reset(reset), .clock(CLK));
  // Probe on treg
  // Probe on T_Reg
  // Probe on S_Reg
  Clock Clock (.out(CLK));
  // Probe on dreg
  // Probe on sreg
  // Probe on treg
  Button u_Reset (.out(reset));

  // Other names for the same wires on the sheet: data[15:0] = Data_Bus

  // Notes on the sheet:
  //   MiMo - Microprogrammed CPU Model
  //   Data BUS
  //   regsrc:	0..DBus 1..IMM 2..ALU 3..Sreg
  //   Destination
  //   v0.4b
  //   Registers
  //   Operands
  //   OR
  //   REZ
  //   OP1
  //   OP2
endmodule

module Registerfile (
  input  [15:0] regval,
  input  Reset,
  input  clock,
  input  dwrite,
  input  swrite,
  input  twrite,
  input  [2:0] dsel,
  input  [2:0] ssel,
  input  [2:0] tsel,
  output [15:0] r0,
  output [15:0] r1,
  output [15:0] r2,
  output [15:0] r3,
  output [15:0] r4,
  output [15:0] r5,
  output [15:0] r6,
  output [15:0] r7,
  output [15:0] dreg,
  output [15:0] sreg,
  output [15:0] treg
);

  wire demultiplexer_1_out0, demultiplexer_1_out1, demultiplexer_1_out2, demultiplexer_1_out3,
       demultiplexer_1_out4, demultiplexer_1_out5, demultiplexer_1_out6, demultiplexer_1_out7;

  Demultiplexer #(.select(3), .enable("false")) demultiplexer_1 (
    .out0(demultiplexer_1_out0), .out1(demultiplexer_1_out1), .out2(demultiplexer_1_out2),
    .out3(demultiplexer_1_out3), .out4(demultiplexer_1_out4), .out5(demultiplexer_1_out5),
    .out6(demultiplexer_1_out6), .out7(demultiplexer_1_out7), .in(dwrite), .sel(dsel));
  Demultiplexer #(.select(3), .enable("false")) demultiplexer_2 (
    .out0(demultiplexer_1_out0), .out1(demultiplexer_1_out1), .out2(demultiplexer_1_out2),
    .out3(demultiplexer_1_out3), .out4(demultiplexer_1_out4), .out5(demultiplexer_1_out5),
    .out6(demultiplexer_1_out6), .out7(demultiplexer_1_out7), .in(swrite), .sel(ssel));
  Demultiplexer #(.select(3), .enable("false")) demultiplexer_3 (
    .out0(demultiplexer_1_out0), .out1(demultiplexer_1_out1), .out2(demultiplexer_1_out2),
    .out3(demultiplexer_1_out3), .out4(demultiplexer_1_out4), .out5(demultiplexer_1_out5),
    .out6(demultiplexer_1_out6), .out7(demultiplexer_1_out7), .in(twrite), .sel(tsel));
  Register #(.width(16)) register_1 (.D(regval), .en(demultiplexer_1_out0), .Q(r0), .clk(clock), .clr(Reset));
  Register #(.width(16)) register_2 (.D(regval), .en(demultiplexer_1_out1), .Q(r1), .clk(clock), .clr(Reset));
  Register #(.width(16)) register_3 (.D(regval), .en(demultiplexer_1_out2), .Q(r2), .clk(clock), .clr(Reset));
  Register #(.width(16)) register_4 (.D(regval), .en(demultiplexer_1_out3), .Q(r3), .clk(clock), .clr(Reset));
  Register #(.width(16)) register_5 (.D(regval), .en(demultiplexer_1_out4), .Q(r4), .clk(clock), .clr(Reset));
  Register #(.width(16)) register_6 (.D(regval), .en(demultiplexer_1_out5), .Q(r5), .clk(clock), .clr(Reset));
  Register #(.width(16)) register_7 (.D(regval), .en(demultiplexer_1_out6), .Q(r6), .clk(clock), .clr(Reset));
  Register #(.width(16)) register_8 (.D(regval), .en(demultiplexer_1_out7), .Q(r7), .clk(clock), .clr(Reset));
  Multiplexer #(.select(3), .width(16), .enable("false")) multiplexer_1 (
    .in0(r0), .in1(r1), .in2(r2), .in3(r3), .in4(r4), .in5(r5), .in6(r6), .in7(r7), .out(dreg), .sel(dsel));
  Multiplexer #(.select(3), .width(16), .enable("false")) multiplexer_2 (
    .in0(r0), .in1(r1), .in2(r2), .in3(r3), .in4(r4), .in5(r5), .in6(r6), .in7(r7), .out(sreg), .sel(ssel));
  Multiplexer #(.select(3), .width(16), .enable("false")) multiplexer_3 (
    .in0(r0), .in1(r1), .in2(r2), .in3(r3), .in4(r4), .in5(r5), .in6(r6), .in7(r7), .out(treg), .sel(tsel));

  // Notes on the sheet:
  //   Register File
endmodule

module ShowHexa (
  input  [15:0] Data,
  output [3:0] Digit,
  output [3:0] Digit_2,
  output [3:0] Digit_3,
  output [3:0] Digit_4
);


  assign Digit = Data[15:12];
  assign Digit_2 = Data[11:8];
  assign Digit_3 = Data[7:4];
  assign Digit_4 = Data[3:0];
endmodule
