// Logisim project mimo_v04b_immed_Demo.circ as structural Verilog: 2 circuits, main circuit MiMo_v04b_OR
// address
module MiMo_v04b_OR (
  input  [15:0] in_1,
  input  imload,
  output [15:0] out_3
);

  wire CLK, reset;

  // Probe on in_1
  Register #(.width(16)) register_1 (.D(in_1), .en(imload), .Q(out_3), .clk(CLK));  // open: clr
  // Probe on out_3
  Clock Clock (.out(CLK));
  Button u_Reset (.out(reset));

  // Other names for the same wires on the sheet: immed[15:0] = out_3; sreg[15:0] = in_1

  // Notes on the sheet:
  //   Data Bus
  //   MiMo - Microprogrammed CPU Model
  //   Imm. Reg.
  //   v0.4b
  //   OR
  //   immed
endmodule

module ShowHexa (
  input  [15:0] Data,
  output [3:0] Digit,
  output [3:0] Digit_2,
  output [3:0] Digit_3,
  output [3:0] Digit_4
);


  assign Digit = Data[15:12];
  assign Digit_2 = Data[11:8];
  assign Digit_3 = Data[7:4];
  assign Digit_4 = Data[3:0];
endmodule
