// Logisim project mimo_v04b_OR.circ as structural Verilog: 8 circuits, main circuit MiMo_v04b_OR
// address
module MiMo_v04b_OR (
  output [7:0] ucounter
);

  wire button_1_out, c, Clear_2_out, Clear_out, CLK, FB_LED, FB_LED2, multiplexer_4_out, n, Ncmd, not_1_out,
       or_1_out, or_2_out, RAM, reset, TTY, twrite, z;
  wire [1:0] addrsel, cond;
  wire [2:0] dregs, sregs, tregs;
  wire [3:0] aluop, icycles, showhexa_1_digit, showhexa_1_digit_2, showhexa_1_digit_3, showhexa_1_digit_4,
       showhexa_2_digit, showhexa_2_digit_2, showhexa_2_digit_3, showhexa_2_digit_4;
  wire [6:0] opcode;
  wire [7:0] adder_1_out, multiplexer_3_out, multiplexer_5_out;
  wire [15:0] address, aluout, cycles, data, dreg, DROM, frame_buffer_16x16_1_out_6,
       frame_buffer_16x16_1_out_7, frame_buffer_16x16_1_out_8, frame_buffer_16x16_1_out_9,
       frame_buffer_16x16_1_out_10, frame_buffer_16x16_1_out_11, frame_buffer_16x16_1_out_12,
       frame_buffer_16x16_1_out_13, frame_buffer_16x16_1_out_14, frame_buffer_16x16_1_out_15,
       frame_buffer_16x16_1_out_16, frame_buffer_16x16_1_out_17, frame_buffer_16x16_1_out_18,
       frame_buffer_16x16_1_out_19, frame_buffer_16x16_1_out_20, frame_buffer_16x16_1_out_21,
       frame_buffer_16x16_2_out_6, frame_buffer_16x16_2_out_7, frame_buffer_16x16_2_out_8,
       frame_buffer_16x16_2_out_9, frame_buffer_16x16_2_out_10, frame_buffer_16x16_2_out_11,
       frame_buffer_16x16_2_out_12, frame_buffer_16x16_2_out_13, frame_buffer_16x16_2_out_14,
       frame_buffer_16x16_2_out_15, frame_buffer_16x16_2_out_16, frame_buffer_16x16_2_out_17,
       frame_buffer_16x16_2_out_18, frame_buffer_16x16_2_out_19, frame_buffer_16x16_2_out_20,
       frame_buffer_16x16_2_out_21, immed, irreg, multiplexer_2_out, multiplexer_6_out, multiplexer_7_out,
       pc, registerfile_1_r0, registerfile_1_r1, registerfile_1_r2, registerfile_1_r3, registerfile_1_r4,
       registerfile_1_r5, registerfile_1_r6, registerfile_1_r7, sreg, treg;
  wire [31:4] CROM;

  Hex_Digit_Display hex_digit_display_1 (.value(showhexa_1_digit));  // open: dp
  ShowHexa showhexa_1 (
    .Digit(showhexa_1_digit), .Digit_2(showhexa_1_digit_2), .Digit_3(showhexa_1_digit_3),
    .Digit_4(showhexa_1_digit_4), .Data(address));
  nor nor_1 (Ncmd, ucounter[0], ucounter[1], ucounter[2], ucounter[3], ucounter[5], ucounter[6], ucounter[7], ucounter[4]);
  Hex_Digit_Display hex_digit_display_2 (.value(showhexa_1_digit_2));  // open: dp
  Hex_Digit_Display hex_digit_display_3 (.value(showhexa_1_digit_3));  // open: dp
  Address_Decoder ADDR_DEC (.Address(address), .output_0(RAM), .output_1(FB_LED), .output_2(TTY), .output_3(FB_LED2));
  // Probe on ucounter
  Register Microcounter (.D(adder_1_out), .Q(ucounter), .clk(CLK), .clr(reset));  // open: en
  Hex_Digit_Display hex_digit_display_4 (.value(showhexa_1_digit_4));  // open: dp
  Hex_Digit_Display hex_digit_display_5 (.value(showhexa_2_digit));  // open: dp
  ShowHexa showhexa_2 (
    .Digit(showhexa_2_digit), .Digit_2(showhexa_2_digit_2), .Digit_3(showhexa_2_digit_3),
    .Digit_4(showhexa_2_digit_4), .Data(data));
  RAM #(.addrWidth(14), .dataWidth(16)) ram_1 (
    .addr(address[13:0]), .data(data), .sel(RAM), .clk(CLK), .ld(not_1_out));  // open: clr
  not not_1 (not_1_out, CROM[6]);
  Hex_Digit_Display hex_digit_display_6 (.value(showhexa_2_digit_2));  // open: dp
  ROM #(.dataWidth(32)) rom_1 (
    .addr(ucounter), .data({CROM[31:19], cond, CROM[16:9], addrsel, CROM[6:4], aluop}));  // open: sel
  ROM #(.dataWidth(16)) rom_2 (.addr(ucounter), .data(DROM));  // open: sel
  // Probe on opcode
  // Probe on address
  Multiplexer #(.select(2), .width(16), .enable("false")) multiplexer_1 (
    .in0(pc), .in1(immed), .in2(aluout), .in3(sreg), .out(address), .sel(addrsel));
  Hex_Digit_Display hex_digit_display_7 (.value(showhexa_2_digit_4));  // open: dp
  Hex_Digit_Display hex_digit_display_8 (.value(showhexa_2_digit_3));  // open: dp
  assign data = CROM[6] ? multiplexer_2_out : 16'bz;  // Controlled_Buffer controlled_buffer_1
  Multiplexer #(.select(2), .width(16), .enable("false")) multiplexer_2 (
    .in0(pc), .in1(dreg), .in2(treg), .in3(aluout), .out(multiplexer_2_out), .sel(CROM[21:20]));
  // Probe on CROM[21:20]
  or or_1 (or_1_out, c, z);
  // Probe on cond
  // Probe on addrsel
  // Probe on DROM[7:0]
  Multiplexer #(.width(8), .enable("false")) multiplexer_3 (
    .in0(DROM[7:0]), .in1(DROM[15:8]), .out(multiplexer_3_out), .sel(multiplexer_4_out));
  // Probe on DROM[15:8]
  Multiplexer #(.select(2), .enable("false")) multiplexer_4 (
    .in0(c), .in1(or_1_out), .in2(z), .in3(n), .out(multiplexer_4_out), .sel(cond));
  Multiplexer #(.width(8), .enable("false")) multiplexer_5 (
    .in0({8{1'b0}}), .in1({1'b0, opcode}), .out(multiplexer_5_out), .sel(CROM[19]));
  Register #(.width(16)) register_1 (.D(data), .en(CROM[14]), .Q(immed), .clk(CLK));  // open: clr
  // Probe on data
  // Probe on adder_1_out
  Adder adder_1 (.a(multiplexer_3_out), .b(multiplexer_5_out), .out(adder_1_out));  // open: cin, cout
  // Probe on pc
  PC pc_1 (.imreg(immed), .sreg(sreg), .pcout(pc), .pcsel(CROM[10:9]), .pcload(CROM[11]), .reset(reset), .clock(CLK));
  // Probe on immed
  Instruction_Register instruction_register_1 (
    .instruction(data), .irload(CROM[13]), .dregsel(dregs), .sregsel(sregs), .tregsel(tregs),
    .opcode(opcode), .Instruction_register(irreg), .reset(reset), .clock(CLK));
  // Probe on irreg
  // Probe on opcode
  // Probe on ucounter
  // Probe on CROM[22]
  // Probe on CROM[21:20]
  Multiplexer #(.select(2), .width(16), .enable("false")) multiplexer_6 (
    .in0(data), .in1(immed), .in2(aluout), .in3(sreg), .out(multiplexer_6_out), .sel(CROM[16:15]));
  // Probe on multiplexer_6_out
  // Probe on CROM[16:15]
  // Probe on cond
  // Probe on CROM[19]
  Counter #(.width(16), .max('hffff), .ongoal("stay")) Cycles_Cnt (
    .Q(cycles), .clk(CLK), .clr(reset));  // open: load, D, count, carry
  Clock Clock (.out(CLK));
  Registerfile registerfile_1 (
    .dwrite(CROM[12]), .regval(multiplexer_6_out), .sreg(sreg), .treg(treg), .dsel(dregs), .ssel(sregs),
    .tsel(tregs), .r0(registerfile_1_r0), .r1(registerfile_1_r1), .r2(registerfile_1_r2),
    .r7(registerfile_1_r7), .r6(registerfile_1_r6), .r5(registerfile_1_r5), .r4(registerfile_1_r4),
    .r3(registerfile_1_r3), .twrite(twrite), .dreg(dreg), .swrite(CROM[22]), .Reset(reset), .clock(CLK));
  // Probe on sregs
  // Probe on dregs
  // Probe on CROM[16:15]
  // Probe on CROM[14]
  Counter #(.width(4), .max('hf), .ongoal("stay")) Instr_Cycles_Cnt (
    .Q(icycles), .clk(CLK), .clr(or_2_out));  // open: load, D, count, carry
  or or_2 (or_2_out, Ncmd, reset);
  // Probe on registerfile_1_r0
  // Probe on registerfile_1_r1
  // Probe on registerfile_1_r2
  // Probe on registerfile_1_r3
  // Probe on registerfile_1_r4
  // Probe on registerfile_1_r5
  // Probe on registerfile_1_r6
  // Probe on registerfile_1_r7
  // Probe on dreg
  // Probe on sreg
  // Probe on treg
  // Probe on tregs
  // Probe on {CROM[31:19], cond, CROM[16:9], addrsel, CROM[6:4], aluop}
  // Probe on CROM[13]
  // Probe on CROM[12]
  Button u_Reset (.out(reset));
  Multiplexer #(.select(2), .width(16), .enable("false")) multiplexer_7 (
    .in0(treg), .in1(immed), .in2({16{1'b0}}), .in3(16'h1), .out(multiplexer_7_out), .sel(CROM[5:4]));
  // Probe on CROM[5:4]
  // Probe on CROM[10:9]
  // Probe on CROM[11]
  ALU alu_1 (.Zero(z), .Negative(n), .Result(aluout), .aluop(aluop), .A(sreg), .B(multiplexer_7_out), .Carry(c));
  // Probe on sreg
  // Probe on multiplexer_7_out
  // Probe on aluop
  // Probe on CROM[6]
  // Probe on addrsel
  // Probe on tregs
  // Probe on opcode
  // Probe on address
  // Probe on aluout
  // Probe on DROM
  // Probe on CROM[5:4]
  // Probe on irreg
  // Probe on dregs
  // Probe on sregs
  // Probe on data
  // Probe on icycles
  // Probe on aluop
  Frame_Buffer_16x16 frame_buffer_16x16_1 (
    .address(address[3:0]), .store(FB_LED2), .data(data), .clock(CLK), .reset(button_1_out),
    .out_6(frame_buffer_16x16_1_out_6), .out_7(frame_buffer_16x16_1_out_7),
    .out_8(frame_buffer_16x16_1_out_8), .out_9(frame_buffer_16x16_1_out_9),
    .out_10(frame_buffer_16x16_1_out_10), .out_11(frame_buffer_16x16_1_out_11),
    .out_12(frame_buffer_16x16_1_out_12), .out_13(frame_buffer_16x16_1_out_13),
    .out_14(frame_buffer_16x16_1_out_14), .out_15(frame_buffer_16x16_1_out_15),
    .out_16(frame_buffer_16x16_1_out_16), .out_17(frame_buffer_16x16_1_out_17),
    .out_18(frame_buffer_16x16_1_out_18), .out_19(frame_buffer_16x16_1_out_19),
    .out_20(frame_buffer_16x16_1_out_20), .out_21(frame_buffer_16x16_1_out_21));
  Frame_Buffer_16x16 frame_buffer_16x16_2 (
    .address(address[3:0]), .store(FB_LED), .data(data), .clock(CLK), .reset(Clear_out),
    .out_6(frame_buffer_16x16_2_out_6), .out_7(frame_buffer_16x16_2_out_7),
    .out_8(frame_buffer_16x16_2_out_8), .out_9(frame_buffer_16x16_2_out_9),
    .out_10(frame_buffer_16x16_2_out_10), .out_11(frame_buffer_16x16_2_out_11),
    .out_12(frame_buffer_16x16_2_out_12), .out_13(frame_buffer_16x16_2_out_13),
    .out_14(frame_buffer_16x16_2_out_14), .out_15(frame_buffer_16x16_2_out_15),
    .out_16(frame_buffer_16x16_2_out_16), .out_17(frame_buffer_16x16_2_out_17),
    .out_18(frame_buffer_16x16_2_out_18), .out_19(frame_buffer_16x16_2_out_19),
    .out_20(frame_buffer_16x16_2_out_20), .out_21(frame_buffer_16x16_2_out_21));
  // Probe on data[6:0]
  // Probe on pc
  // Probe on irreg
  // Probe on immed
  // Probe on aluout
  LED u_C (.in(c));
  LED u_Z (.in(z));
  LED u_N (.in(n));
  LED New_CMD (.in(Ncmd));
  // Probe on cycles
  DotMatrix #(.inputtype("row"), .matrixcols(16), .matrixrows(16)) dotmatrix_1 (
    .row0(frame_buffer_16x16_1_out_21), .row1(frame_buffer_16x16_1_out_20),
    .row2(frame_buffer_16x16_1_out_19), .row3(frame_buffer_16x16_1_out_18),
    .row4(frame_buffer_16x16_1_out_17), .row5(frame_buffer_16x16_1_out_16),
    .row6(frame_buffer_16x16_1_out_15), .row7(frame_buffer_16x16_1_out_14),
    .row8(frame_buffer_16x16_1_out_13), .row9(frame_buffer_16x16_1_out_12),
    .row10(frame_buffer_16x16_1_out_11), .row11(frame_buffer_16x16_1_out_10),
    .row12(frame_buffer_16x16_1_out_9), .row13(frame_buffer_16x16_1_out_8),
    .row14(frame_buffer_16x16_1_out_7), .row15(frame_buffer_16x16_1_out_6));
  Button button_1 (.out(button_1_out));
  DotMatrix #(.inputtype("row"), .matrixcols(16), .matrixrows(16)) dotmatrix_2 (
    .row0(frame_buffer_16x16_2_out_21), .row1(frame_buffer_16x16_2_out_20),
    .row2(frame_buffer_16x16_2_out_19), .row3(frame_buffer_16x16_2_out_18),
    .row4(frame_buffer_16x16_2_out_17), .row5(frame_buffer_16x16_2_out_16),
    .row6(frame_buffer_16x16_2_out_15), .row7(frame_buffer_16x16_2_out_14),
    .row8(frame_buffer_16x16_2_out_13), .row9(frame_buffer_16x16_2_out_12),
    .row10(frame_buffer_16x16_2_out_11), .row11(frame_buffer_16x16_2_out_10),
    .row12(frame_buffer_16x16_2_out_9), .row13(frame_buffer_16x16_2_out_8),
    .row14(frame_buffer_16x16_2_out_7), .row15(frame_buffer_16x16_2_out_6));
  TTY #(.rows(4), .cols(16)) tty_1 (.data(data[6:0]), .clk(CLK), .we(TTY), .clr(Clear_2_out));
  Button Clear (.out(Clear_out));
  Button Clear_2 (.out(Clear_2_out));

  // Other names for the same wires on the sheet: CROM (some bits) = {cond, addrsel, aluop}; op2sel[1:0] = CROM[5:4];
  //   datawrite = CROM[6]; pcsel[1:0] = CROM[10:9]; pcload = CROM[11]; dwrite = CROM[12]; irload = CROM[13];
  //   imload = CROM[14]; regsrc[1:0] = CROM[16:15]; indexsel = CROM[19]; datasel[1:0] = CROM[21:20];
  //   swrite = CROM[22]; MicroPC[7:0] = ucounter

  // Notes on the sheet:
  //   Address BUS
  //   RAM
  //   Control ROM
  //   Address of first uinstruction is "opcode+2"
  //   MiMo - Microprogrammed CPU Model
  //   Data BUS
  //   Microcode Control Unit
  //   contents of rom_1 (hex, n*v repeats v):
  //   2000 80800 11000 11001 11002 11003 11004 11005 11006 11007 11008 11009 1100a 1100b 1100c 1100d 1100e
  //   1100f 15*4000 0 0 4000 6*0 4000 22*0 1000 4000 4000 4*0 19000 410025 41000a 55*0 11010 11011 11012
  //   11013 11014 11015 11016 11017 11018 11019 1101b 1101c 1101d 1101e 1101f 40001 40021 1080 1000c0
  //   410030 800 a00
  //   Decision ROM
  //   contents of rom_2 (hex, n*v repeats v):
  //   101 202 16*0 8282 8383 8484 8585 8686 8787 8888 8989 8a8a 8b8b 8c8c 8d8d 8e8e 8f8f 9090 0 0 9191 6*0
  //   9292 22*0 9696 9393 9494 6*0 9595 55*0 15*9696 9796 9697 9696 9696
  //   Imm. Reg.
  //   v0.4b
  //   PC
  //   Ins.Reg.
  //   OR
  //   Based on: http://minnie.tuhs.org/Programs/UcodeCPU/index.html
  //   v04: Tidying up model, FB, TTY
  //   v03b: Fix z cond code
  //   Quick tips:
  //   2a [42]:	addrsel=pc  imload=1   # JNEZ Rs,immed
  //   84 [132]:   pcincr:	 pcload=1  pcsel=pc, goto fetch
  //   85 [133]:   jump:	  pcload=1  pcsel=immed, goto fetch
  //   Registers
  //   41 [65]:	addrsel=pc  dwrite=1  regsrc=databus  # Load immediate Rd, immed
  //   43 [67]:	addrsel=pc  imload=1    # Store Rd into address from immed
  //   Micro Instruction
  //   Use ctrl+t to manually toggle global clock signal
  //   Use Simulate->Ticks Enabled for automatic clock signal
  //   2:	aluop=add  op2sel=treg  dwrite=1  regsrc=aluout, goto fetch  # ALU operations on Rd,Rs,Rt
  //   ALU
  //   Instruction:
  //   Address, Data Bus
  //   Spec. Registers
  //   TTY
  //   Flags
  //   Status
  //   Frame Buffer LED 16x16
endmodule

module Instruction_Register (
  input  [15:0] instruction,
  input  reset,
  input  clock,
  input  irload,
  output [2:0] dregsel,
  output [2:0] sregsel,
  output [2:0] tregsel,
  output [6:0] opcode,
  output [15:0] Instruction_register
);

  Register #(.width(16)) IR (
    .D(instruction), .en(irload), .Q({Instruction_register[15:3], dregsel}), .clk(clock), .clr(reset));

  assign Instruction_register[2:0] = dregsel;
  assign opcode = Instruction_register[15:9];
  assign sregsel = Instruction_register[5:3];
  assign tregsel = Instruction_register[8:6];

  // Notes on the sheet:
  //   IR Logic
endmodule

module Registerfile (
  input  [15:0] regval,
  input  Reset,
  input  clock,
  input  dwrite,
  input  swrite,
  input  twrite,
  input  [2:0] dsel,
  input  [2:0] ssel,
  input  [2:0] tsel,
  output [15:0] r0,
  output [15:0] r1,
  output [15:0] r2,
  output [15:0] r3,
  output [15:0] r4,
  output [15:0] r5,
  output [15:0] r6,
  output [15:0] r7,
  output [15:0] dreg,
  output [15:0] sreg,
  output [15:0] treg
);

  wire demultiplexer_1_out0, demultiplexer_1_out1, demultiplexer_1_out2, demultiplexer_1_out3,
       demultiplexer_1_out4, demultiplexer_1_out5, demultiplexer_1_out6, demultiplexer_1_out7;

  Demultiplexer #(.select(3), .enable("false")) demultiplexer_1 (
    .out0(demultiplexer_1_out0), .out1(demultiplexer_1_out1), .out2(demultiplexer_1_out2),
    .out3(demultiplexer_1_out3), .out4(demultiplexer_1_out4), .out5(demultiplexer_1_out5),
    .out6(demultiplexer_1_out6), .out7(demultiplexer_1_out7), .in(dwrite), .sel(dsel));
  Demultiplexer #(.select(3), .enable("false")) demultiplexer_2 (
    .out0(demultiplexer_1_out0), .out1(demultiplexer_1_out1), .out2(demultiplexer_1_out2),
    .out3(demultiplexer_1_out3), .out4(demultiplexer_1_out4), .out5(demultiplexer_1_out5),
    .out6(demultiplexer_1_out6), .out7(demultiplexer_1_out7), .in(swrite), .sel(ssel));
  Demultiplexer #(.select(3), .enable("false")) demultiplexer_3 (
    .out0(demultiplexer_1_out0), .out1(demultiplexer_1_out1), .out2(demultiplexer_1_out2),
    .out3(demultiplexer_1_out3), .out4(demultiplexer_1_out4), .out5(demultiplexer_1_out5),
    .out6(demultiplexer_1_out6), .out7(demultiplexer_1_out7), .in(twrite), .sel(tsel));
  Register #(.width(16)) register_1 (.D(regval), .en(demultiplexer_1_out0), .Q(r0), .clk(clock), .clr(Reset));
  Register #(.width(16)) register_2 (.D(regval), .en(demultiplexer_1_out1), .Q(r1), .clk(clock), .clr(Reset));
  Register #(.width(16)) register_3 (.D(regval), .en(demultiplexer_1_out2), .Q(r2), .clk(clock), .clr(Reset));
  Register #(.width(16)) register_4 (.D(regval), .en(demultiplexer_1_out3), .Q(r3), .clk(clock), .clr(Reset));
  Register #(.width(16)) register_5 (.D(regval), .en(demultiplexer_1_out4), .Q(r4), .clk(clock), .clr(Reset));
  Register #(.width(16)) register_6 (.D(regval), .en(demultiplexer_1_out5), .Q(r5), .clk(clock), .clr(Reset));
  Register #(.width(16)) register_7 (.D(regval), .en(demultiplexer_1_out6), .Q(r6), .clk(clock), .clr(Reset));
  Register #(.width(16)) register_8 (.D(regval), .en(demultiplexer_1_out7), .Q(r7), .clk(clock), .clr(Reset));
  Multiplexer #(.select(3), .width(16), .enable("false")) multiplexer_1 (
    .in0(r0), .in1(r1), .in2(r2), .in3(r3), .in4(r4), .in5(r5), .in6(r6), .in7(r7), .out(dreg), .sel(dsel));
  Multiplexer #(.select(3), .width(16), .enable("false")) multiplexer_2 (
    .in0(r0), .in1(r1), .in2(r2), .in3(r3), .in4(r4), .in5(r5), .in6(r6), .in7(r7), .out(sreg), .sel(ssel));
  Multiplexer #(.select(3), .width(16), .enable("false")) multiplexer_3 (
    .in0(r0), .in1(r1), .in2(r2), .in3(r3), .in4(r4), .in5(r5), .in6(r6), .in7(r7), .out(treg), .sel(tsel));

  // Notes on the sheet:
  //   Register File
endmodule

module ALU (
  input  [15:0] A,
  input  [15:0] B,
  input  [3:0] aluop,
  output Carry,
  output Zero,
  output Negative,
  output [15:0] Result
);

  wire adder_1_cout, or_2_out, subtractor_1_bout;
  wire [15:0] adder_1_out, and_1_out, divider_1_out, divider_1_rem, multiplier_1_out, nand_1_out, nor_1_out,
       not_1_out, or_1_out, shifter_1_out, shifter_2_out, shifter_3_out, shifter_4_out, shifter_5_out,
       subtractor_1_out, xor_1_out;

  Adder #(.width(16)) adder_1 (.a(A), .b(B), .out(adder_1_out), .cin(1'b0), .cout(adder_1_cout));
  Subtractor #(.width(16)) subtractor_1 (.a(A), .b(B), .out(subtractor_1_out), .bin(1'b0), .bout(subtractor_1_bout));
  Multiplier #(.width(16)) multiplier_1 (.a(A), .b(B), .out(multiplier_1_out), .cin({16{1'b0}}));  // open: cout
  Divider #(.width(16)) divider_1 (.a(A), .b(B), .out(divider_1_out), .upper({16{1'b0}}), .rem(divider_1_rem));
  assign and_1_out = A & B;  // AND_Gate and_1, 16 bits wide
  assign or_1_out = A | B;  // OR_Gate or_1, 16 bits wide
  assign xor_1_out = A ^ B;  // XOR_Gate xor_1, 16 bits wide
  assign nand_1_out = ~(A & B);  // NAND_Gate nand_1, 16 bits wide
  assign nor_1_out = ~(A | B);  // NOR_Gate nor_1, 16 bits wide
  assign not_1_out = ~A;  // NOT_Gate not_1, 16 bits wide
  Shifter #(.width(16)) shifter_1 (.in(A), .\dist (B[3:0]), .out(shifter_1_out));
  Shifter #(.width(16), .shift("lr")) shifter_2 (.in(A), .\dist (B[3:0]), .out(shifter_2_out));
  Shifter #(.width(16), .shift("ar")) shifter_3 (.in(A), .\dist (B[3:0]), .out(shifter_3_out));
  Shifter #(.width(16), .shift("rl")) shifter_4 (.in(A), .\dist (B[3:0]), .out(shifter_4_out));
  Shifter #(.width(16), .shift("rr")) shifter_5 (.in(A), .\dist (B[3:0]), .out(shifter_5_out));
  Multiplexer #(.select(4), .width(16), .enable("false")) multiplexer_1 (
    .in0(adder_1_out), .in1(subtractor_1_out), .in2(multiplier_1_out), .in3(divider_1_out),
    .in4(divider_1_rem), .in5(and_1_out), .in6(or_1_out), .in7(xor_1_out), .in8(nand_1_out), .in9(nor_1_out),
    .in10(not_1_out), .in11(shifter_1_out), .in12(shifter_2_out), .in13(shifter_3_out), .in14(shifter_4_out),
    .in15(shifter_5_out), .out({Negative, Result[14:0]}), .sel(aluop));
  Multiplexer #(.select(4), .enable("false")) multiplexer_2 (
    .in0(adder_1_cout), .in1(subtractor_1_bout), .in2(1'b0), .in3(1'b0), .in4(1'b0), .in5(1'b0), .in6(1'b0),
    .in7(1'b0), .in8(1'b0), .in9(1'b0), .in10(1'b0), .in11(1'b0), .in12(1'b0), .in13(1'b0), .in14(1'b0),
    .in15(1'b0), .out(Carry), .sel(aluop));
  not not_2 (Zero, or_2_out);
  or or_2 (or_2_out, Result[0], Result[1], Result[2], Result[3], Result[4], Result[5], Result[6], Result[7], Result[9], Result[10], Result[11], Result[12], Result[13], Result[14], Negative, Result[8]);

  assign Result[15] = Negative;

  // Notes on the sheet:
  //   16-bit ALU
endmodule

module PC (
  input  [15:0] imreg,
  input  pcload,
  input  clock,
  input  reset,
  input  [15:0] sreg,
  input  [1:0] pcsel,
  output [15:0] pcout
);

  wire [15:0] adder_1_out, adder_2_out, multiplexer_1_out;

  Adder #(.width(16)) adder_1 (.a(pcout), .b(16'h1), .out(adder_1_out));  // open: cin, cout
  Adder #(.width(16)) adder_2 (.a(pcout), .b(imreg), .out(adder_2_out));  // open: cin, cout
  Multiplexer #(.select(2), .width(16), .enable("false")) multiplexer_1 (
    .in0(adder_1_out), .in1(imreg), .in2(adder_2_out), .in3(sreg), .out(multiplexer_1_out), .sel(pcsel));
  Register #(.width(16)) PC (.D(multiplexer_1_out), .en(pcload), .Q(pcout), .clk(clock), .clr(reset));

  // Notes on the sheet:
  //   PC Logic
endmodule

module ShowHexa (
  input  [15:0] Data,
  output [3:0] Digit,
  output [3:0] Digit_2,
  output [3:0] Digit_3,
  output [3:0] Digit_4
);


  assign Digit = Data[15:12];
  assign Digit_2 = Data[11:8];
  assign Digit_3 = Data[7:4];
  assign Digit_4 = Data[3:0];
endmodule

module Frame_Buffer_16x16 (
  input  [3:0] address,
  input  store,
  input  [15:0] data,
  input  clock,
  input  reset,
  output [15:0] out_6,
  output [15:0] out_7,
  output [15:0] out_8,
  output [15:0] out_9,
  output [15:0] out_10,
  output [15:0] out_11,
  output [15:0] out_12,
  output [15:0] out_13,
  output [15:0] out_14,
  output [15:0] out_15,
  output [15:0] out_16,
  output [15:0] out_17,
  output [15:0] out_18,
  output [15:0] out_19,
  output [15:0] out_20,
  output [15:0] out_21
);

  wire demultiplexer_1_out0, demultiplexer_1_out1, demultiplexer_1_out2, demultiplexer_1_out3,
       demultiplexer_1_out4, demultiplexer_1_out5, demultiplexer_1_out6, demultiplexer_1_out7,
       demultiplexer_1_out8, demultiplexer_1_out9, demultiplexer_1_out10, demultiplexer_1_out11,
       demultiplexer_1_out12, demultiplexer_1_out13, demultiplexer_1_out14, demultiplexer_1_out15;

  Demultiplexer #(.select(4), .enable("false")) demultiplexer_1 (
    .out0(demultiplexer_1_out0), .out1(demultiplexer_1_out1), .out2(demultiplexer_1_out2),
    .out3(demultiplexer_1_out3), .out4(demultiplexer_1_out4), .out5(demultiplexer_1_out5),
    .out6(demultiplexer_1_out6), .out7(demultiplexer_1_out7), .out8(demultiplexer_1_out8),
    .out9(demultiplexer_1_out9), .out10(demultiplexer_1_out10), .out11(demultiplexer_1_out11),
    .out12(demultiplexer_1_out12), .out13(demultiplexer_1_out13), .out14(demultiplexer_1_out14),
    .out15(demultiplexer_1_out15), .in(store), .sel(address));
  Register #(.width(16)) register_1 (.D(data), .en(demultiplexer_1_out0), .Q(out_6), .clk(clock), .clr(reset));
  Register #(.width(16)) register_2 (.D(data), .en(demultiplexer_1_out1), .Q(out_7), .clk(clock), .clr(reset));
  Register #(.width(16)) register_3 (.D(data), .en(demultiplexer_1_out2), .Q(out_8), .clk(clock), .clr(reset));
  Register #(.width(16)) register_4 (.D(data), .en(demultiplexer_1_out3), .Q(out_9), .clk(clock), .clr(reset));
  Register #(.width(16)) register_5 (.D(data), .en(demultiplexer_1_out4), .Q(out_10), .clk(clock), .clr(reset));
  Register #(.width(16)) register_6 (.D(data), .en(demultiplexer_1_out5), .Q(out_11), .clk(clock), .clr(reset));
  Register #(.width(16)) register_7 (.D(data), .en(demultiplexer_1_out6), .Q(out_12), .clk(clock), .clr(reset));
  Register #(.width(16)) register_8 (.D(data), .en(demultiplexer_1_out7), .Q(out_13), .clk(clock), .clr(reset));
  Register #(.width(16)) register_9 (.D(data), .en(demultiplexer_1_out8), .Q(out_14), .clk(clock), .clr(reset));
  Register #(.width(16)) register_10 (.D(data), .en(demultiplexer_1_out9), .Q(out_15), .clk(clock), .clr(reset));
  Register #(.width(16)) register_11 (.D(data), .en(demultiplexer_1_out10), .Q(out_16), .clk(clock), .clr(reset));
  Register #(.width(16)) register_12 (.D(data), .en(demultiplexer_1_out11), .Q(out_17), .clk(clock), .clr(reset));
  Register #(.width(16)) register_13 (.D(data), .en(demultiplexer_1_out12), .Q(out_18), .clk(clock), .clr(reset));
  Register #(.width(16)) register_14 (.D(data), .en(demultiplexer_1_out13), .Q(out_19), .clk(clock), .clr(reset));
  Register #(.width(16)) register_15 (.D(data), .en(demultiplexer_1_out14), .Q(out_20), .clk(clock), .clr(reset));
  Register #(.width(16)) register_16 (.D(data), .en(demultiplexer_1_out15), .Q(out_21), .clk(clock), .clr(reset));
endmodule

module Address_Decoder (
  input  [15:0] Address,
  output output_0,
  output output_1,
  output output_2,
  output output_3
);

  wire not_1_out, not_2_out;

  not not_1 (not_1_out, Address[14]);
  not not_2 (not_2_out, Address[15]);
  and and_1 (output_0, not_1_out, not_2_out);
  and and_2 (output_1, Address[14], not_2_out);
  and and_3 (output_2, not_1_out, Address[15]);
  and and_4 (output_3, Address[14], Address[15]);
endmodule
